// Logisim project datapath.circ as structural Verilog: 1 circuit, main circuit main
module main (
);

  wire and_1_out, Clock, mips_alu_1_p3, mips_alu_1_p4, registerfile_1_p4;
  wire [4:0] multiplexer_1_out;
  wire [5:0] Control_p2;
  wire [7:0] adder_2_out, bit_extender_1_out, bit_extender_3_out, shifter_1_out;
  wire [8:0] Control_p3;
  wire [23:0] mips_alu_1_p5;
  wire [25:0] mipsprogramrom_1_p1;
  wire [31:0] adder_1_out, adder_3_out, bit_extender_2_out, mips_ram_1_p3, mipsprogramrom_1_p2,
       multiplexer_2_out, multiplexer_3_out, PC_q, registerfile_1_p5, shifter_2_out;
  wire [31:24] mips_alu_1_p5_2;

  Clock clock_1 (.out(Clock));
  Register #(.width(32)) PC (.D(multiplexer_3_out), .Q(PC_q), .clk(Clock));  // open: en, clr
  Adder #(.width(32)) adder_1 (.a(32'h4), .b(PC_q), .out(adder_1_out));  // open: cin, cout
  // PLA Control: pin names not known; wires that end beside it: PC_q, Control_p2, Control_p3
  // MIPSProgramROM mipsprogramrom_1: pin names not known; wires that end beside it: {Control_p2, mipsprogramrom_1_p1}, mipsprogramrom_1_p2, Clock, Control_p3[5]
  assign bit_extender_1_out = {{6{1'b0}}, Control_p3[1:0]};  // Bit_Extender bit_extender_1
  Multiplexer #(.width(5), .enable("false")) multiplexer_1 (
    .in0(mipsprogramrom_1_p1[20:16]), .in1(mipsprogramrom_1_p1[15:11]), .out(multiplexer_1_out),
    .sel(Control_p3[8]));
  Shifter shifter_1 (.in(bit_extender_1_out), .\dist (3'b110), .out(shifter_1_out));
  // RegisterFile registerfile_1: pin names not known; wires that end beside it: multiplexer_1_out, mipsprogramrom_1_p1[25:21], mipsprogramrom_1_p1[20:16], registerfile_1_p4, registerfile_1_p5, registerfile_1_p5
  assign bit_extender_2_out = {{16{mipsprogramrom_1_p1[15]}}, mipsprogramrom_1_p1[15:0]};  // Bit_Extender bit_extender_2
  assign bit_extender_3_out = {{2{1'b0}}, mipsprogramrom_1_p1[5:0]};  // Bit_Extender bit_extender_3
  Shifter #(.width(32)) shifter_2 (.in(bit_extender_2_out), .\dist (5'b00010), .out(shifter_2_out));
  Multiplexer #(.width(32), .enable("false")) multiplexer_2 (
    .in0(registerfile_1_p5), .in1(bit_extender_2_out), .out(multiplexer_2_out), .sel(Control_p3[7]));
  Adder adder_2 (.a(bit_extender_3_out), .b(shifter_1_out), .out(adder_2_out));  // open: cin, cout
  Adder #(.width(32)) adder_3 (.a(adder_1_out), .b(shifter_2_out), .out(adder_3_out));  // open: cin, cout
  // MIPS_ALU mips_alu_1: pin names not known; wires that end beside it: registerfile_1_p4, multiplexer_2_out, mips_alu_1_p3, mips_alu_1_p4, {mips_alu_1_p5_2, mips_alu_1_p5}
  // PLA ALU_control: pin names not known; wires that end beside it: adder_2_out, mips_alu_1_p3, registerfile_1_p5, Control_p3[3], Control_p3[4]
  Multiplexer #(.width(32), .enable("false")) multiplexer_3 (
    .in0(adder_1_out), .in1(adder_3_out), .out(multiplexer_3_out), .sel(and_1_out));
  and and_1 (and_1_out, Control_p3[2], mips_alu_1_p4);
  // MIPS_RAM mips_ram_1: pin names not known; wires that end beside it: mips_alu_1_p5, Clock, mips_ram_1_p3
  Multiplexer #(.width(32), .enable("false")) multiplexer_4 (
    .in0(mips_ram_1_p3), .in1({mips_alu_1_p5_2, mips_alu_1_p5}), .out(mipsprogramrom_1_p2),
    .sel(Control_p3[6]));
endmodule
