// Logisim project mips.circ as structural Verilog: 2 circuits, main circuit main
module main (
);

  wire Clock;
  wire [4:0] bitselector_1_out, pla_1_p2;
  wire [31:0] mipsprogramrom_1_p2, pc_1_pc_value;

  Clock clock_1 (.out(Clock));
  PC pc_1 (.Clock(Clock), .PC_value(pc_1_pc_value));
  // MIPSProgramROM mipsprogramrom_1: pin names not known; wires that end beside it: pc_1_pc_value, mipsprogramrom_1_p2, mipsprogramrom_1_p2[15:0]
  // PLA pla_1: pin names not known; wires that end beside it: mipsprogramrom_1_p2[31:26], pla_1_p2
  BitSelector #(.width(16), .group(5)) bitselector_1 (
    .in(mipsprogramrom_1_p2[15:0]), .out(bitselector_1_out), .sel(2'b11));
  Multiplexer #(.width(5), .enable("false")) multiplexer_1 (
    .in0(mipsprogramrom_1_p2[20:16]), .in1(bitselector_1_out), .out(pla_1_p2));  // open: sel
  // RegisterFile registerfile_1: pin names not known; wires that end beside it: mipsprogramrom_1_p2[25:21], mipsprogramrom_1_p2[20:16]
endmodule

module PC (
  input  Clock,
  output [31:0] PC_value
);

  wire [31:0] adder_1_p3;

  // Adder adder_1: pin names not known; wires that end beside it: PC_value, 32'h4, adder_1_p3
  Register #(.width(32)) register_1 (.D(adder_1_p3), .Q(PC_value), .clk(Clock));  // open: en, clr
endmodule
